// Logisim project ALU_8_bit.circ as structural Verilog: 8 circuits, main circuit one_bit_mem
module one_bit_mem (
  input  data,
  input  store,
  output O
);

  wire and_1_out, and_2_out, nor_1_out, not_1_out;

  and and_1 (and_1_out, data, store);
  and and_2 (and_2_out, store, not_1_out);
  not not_1 (not_1_out, data);
  nor nor_1 (nor_1_out, and_1_out, O);
  nor nor_2 (O, nor_1_out, and_2_out);
endmodule

// t
module testB (
  input  in_1,
  input  in_2,
  input  in_3
);
endmodule

module one_byte_mem (
  input  Set,
  input  Enable,
  input  [7:0] Data,
  output [7:0] DataOut
);

  wire [7:0] one_bit_mem_1_o;

  one_bit_mem one_bit_mem_1 (.data(Data[0]), .store(Set), .O(one_bit_mem_1_o[0]));
  one_bit_mem one_bit_mem_2 (.data(Data[1]), .store(Set), .O(one_bit_mem_1_o[1]));
  one_bit_mem one_bit_mem_3 (.data(Data[2]), .store(Set), .O(one_bit_mem_1_o[2]));
  one_bit_mem one_bit_mem_4 (.data(Data[3]), .store(Set), .O(one_bit_mem_1_o[3]));
  one_bit_mem one_bit_mem_5 (.data(Data[4]), .store(Set), .O(one_bit_mem_1_o[4]));
  one_bit_mem one_bit_mem_6 (.data(Data[5]), .store(Set), .O(one_bit_mem_1_o[5]));
  one_bit_mem one_bit_mem_7 (.data(Data[6]), .store(Set), .O(one_bit_mem_1_o[6]));
  one_bit_mem one_bit_mem_8 (.data(Data[7]), .store(Set), .O(one_bit_mem_1_o[7]));
  assign DataOut = Enable ? one_bit_mem_1_o : 8'bz;  // Controlled_Buffer controlled_buffer_1
endmodule

module ALU (
  input  [3:0] Opcode,
  input  Enable,
  input  [7:0] A,
  input  [7:0] B,
  output [7:0] C,
  output [3:0] Flags
);

  wire and_1_out, and_2_out, and_3_out, math_1_carryout, nor_1_out, not_1_out, not_2_out, rotate_1_carryout;
  wire [7:0] logic_1_c, math_1_c, multiplexer_1_out, multiplexer_2_out, rotate_1_c;

  and and_1 (and_1_out, Opcode[2], Opcode[3]);
  Multiplexer #(.width(8)) multiplexer_1 (.in0(B), .in1(8'h1), .out(multiplexer_1_out), .sel(and_1_out));
  and and_2 (and_2_out, Opcode[2], Opcode[1], Opcode[0]);
  not not_1 (not_1_out, and_2_out);
  Math math_1 (
    .Carry(Opcode[0]), .Negate(Opcode[1]), .B(A), .A(multiplexer_1_out), .C(math_1_c),
    .CarryOut(math_1_carryout));
  Logic logic_1 (.data1(Opcode[0]), .data2(Opcode[1]), .A(A), .B(multiplexer_1_out), .C(logic_1_c));
  Rotate rotate_1 (.left_right(Opcode[0]), .carry(Opcode[1]), .A(A), .C(rotate_1_c), .carryOut(rotate_1_carryout));
  and and_3 (and_3_out, not_1_out, Enable);
  assign C = and_3_out ? multiplexer_2_out : 8'bz;  // Controlled_Buffer controlled_buffer_1
  Multiplexer #(.select(2), .width(8)) multiplexer_2 (
    .in0(math_1_c), .in1(logic_1_c), .in2(rotate_1_c), .in3(math_1_c), .out(multiplexer_2_out),
    .sel(Opcode[3:2]));
  nor nor_1 (nor_1_out, multiplexer_2_out[1], multiplexer_2_out[2], multiplexer_2_out[3], multiplexer_2_out[4], multiplexer_2_out[5], multiplexer_2_out[6], multiplexer_2_out[7]);
  Multiplexer #(.select(2)) multiplexer_3 (
    .in0(math_1_carryout), .in1(1'b0), .in2(rotate_1_carryout), .in3(1'b0), .out(Flags[3]), .sel(Opcode[3:2]));
  not not_2 (not_2_out, multiplexer_2_out[0]);
  and and_4 (Flags[2], not_2_out, nor_1_out);
  and and_5 (Flags[1], nor_1_out, multiplexer_2_out[0]);
  not not_3 (Flags[0], multiplexer_2_out[0]);

  // Notes on the sheet:
  //   Carry
  //   Zero
  //   One
  //   Even
endmodule

module full_ADD_SUB_one_bit (
  input  A,
  input  B,
  input  C,
  input  Negate,
  output O,
  output Carry
);

  wire and_1_out, and_2_out, and_3_out, xor_1_out, xor_2_out;

  xor xor_1 (xor_1_out, Negate, A);
  xor xor_2 (xor_2_out, A, B);
  xor xor_3 (O, xor_2_out, C);
  and and_1 (and_1_out, B, C);
  and and_2 (and_2_out, C, xor_1_out);
  and and_3 (and_3_out, B, xor_1_out);
  or or_1 (Carry, and_1_out, and_2_out, and_3_out);

  // Notes on the sheet:
  //   N = 0 : A+B+C
  //   N = 1 : A-B-C
endmodule

module Math (
  input  Carry,
  input  Negate,
  input  [7:0] B,
  input  [7:0] A,
  output [7:0] C,
  output CarryOut
);

  wire full_add_sub_one_bit_1_carry, full_add_sub_one_bit_2_carry, full_add_sub_one_bit_3_carry,
       full_add_sub_one_bit_4_carry, full_add_sub_one_bit_5_carry, full_add_sub_one_bit_6_carry,
       full_add_sub_one_bit_7_carry;

  full_ADD_SUB_one_bit full_add_sub_one_bit_1 (
    .A(B[0]), .B(A[0]), .C(Carry), .Negate(Negate), .O(C[0]), .Carry(full_add_sub_one_bit_1_carry));
  full_ADD_SUB_one_bit full_add_sub_one_bit_2 (
    .A(B[1]), .B(A[1]), .C(full_add_sub_one_bit_1_carry), .Negate(Negate), .O(C[1]),
    .Carry(full_add_sub_one_bit_2_carry));
  full_ADD_SUB_one_bit full_add_sub_one_bit_3 (
    .A(B[2]), .B(A[2]), .C(full_add_sub_one_bit_2_carry), .Negate(Negate), .O(C[2]),
    .Carry(full_add_sub_one_bit_3_carry));
  full_ADD_SUB_one_bit full_add_sub_one_bit_4 (
    .A(B[3]), .B(A[3]), .C(full_add_sub_one_bit_3_carry), .Negate(Negate), .O(C[3]),
    .Carry(full_add_sub_one_bit_4_carry));
  full_ADD_SUB_one_bit full_add_sub_one_bit_5 (
    .A(B[4]), .B(A[4]), .C(full_add_sub_one_bit_4_carry), .Negate(Negate), .O(C[4]),
    .Carry(full_add_sub_one_bit_5_carry));
  full_ADD_SUB_one_bit full_add_sub_one_bit_6 (
    .A(B[5]), .B(A[5]), .C(full_add_sub_one_bit_5_carry), .Negate(Negate), .O(C[5]),
    .Carry(full_add_sub_one_bit_6_carry));
  full_ADD_SUB_one_bit full_add_sub_one_bit_7 (
    .A(B[6]), .B(A[6]), .C(full_add_sub_one_bit_6_carry), .Negate(Negate), .O(C[6]),
    .Carry(full_add_sub_one_bit_7_carry));
  full_ADD_SUB_one_bit full_add_sub_one_bit_8 (
    .A(B[7]), .B(A[7]), .C(full_add_sub_one_bit_7_carry), .Negate(Negate), .O(C[7]), .Carry(CarryOut));
endmodule

module Rotate (
  input  left_right,
  input  carry,
  input  [7:0] A,
  output [7:0] C,
  output carryOut
);

  Multiplexer #(.width(8)) multiplexer_1 (.in0({A[6:0], carry}), .in1({carry, A[7:1]}), .out(C), .sel(left_right));
  Multiplexer multiplexer_2 (.in0(A[7]), .in1(A[0]), .out(carryOut), .sel(left_right));

  // Notes on the sheet:
  //   data1 = left or right // data2 = with or without carry
endmodule

module Logic (
  input  data1,
  input  data2,
  input  [7:0] A,
  input  [7:0] B,
  output [7:0] C
);

  wire [7:0] and_1_out, or_1_out, xor_1_out;

  assign and_1_out = A & B;  // AND_Gate and_1, 8 bits wide
  assign xor_1_out = A ^ B;  // XOR_Gate xor_1, 8 bits wide
  assign or_1_out = A | B;  // OR_Gate or_1, 8 bits wide
  Multiplexer #(.select(2), .width(8)) multiplexer_1 (
    .in0(and_1_out), .in1(xor_1_out), .in2(or_1_out), .out(C), .sel({data2, data1}));  // open: in3
endmodule
